# Fritzing sketch pico-buzzer (saved by Fritzing 0.9.4)
breadboards: 1

parts:
  Mod1 = Raspberry Pi Pico
  J1 = Piezo Speaker
  S1 = Pushbutton [package="[SMD]"]
  USBTTL1 = Micro USB B Plug  # not connected

nets:
  N1: Mod1.pin_3, Mod1.pin_8, Mod1.pin_13, Mod1.pin_18, Mod1.pin_23, Mod1.pin_28, Mod1.pin_33, Mod1.pin_38, J1.pin1, S1.Pin_3, S1.Pin_4
  N2: Mod1.pin_20, S1.Pin_1, S1.Pin_2
  N3: Mod1.pin_26, J1.pin2

custom parts:
  Raspberry Pi Pico: Raspberry Pi Pico. Based around the RP2040 microcontroller the Pico is a low cost microcontroller device bringing Raspberry Pi quality, cost, and easy of use to the microcontroller space. Jan 2021, Split part in to two versions: tht (this one) and SMD. This one will drill holes for a .1 in header in pcb to allow plugging in the module as well as providing pads to solder the module to the top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
